# Fritzing sketch Garden_water (saved by Fritzing 0.9.3b)

parts:
  LED1 = RGB LED (com. cathode, rgb) [package="5 mm [THT]"]
  part = ESP8266 WiFi Module [part_number=ESP8266]
  R1 = Resistor [tolerance=±5% resistance=330 package=THT]
  R2 = Resistor [tolerance=±5% resistance=330 package=THT]
  R3 = Resistor [tolerance=±5% resistance=330 package=THT]
  DHT1 = DHT11 Humitidy and Temperature Sensor
  DHT2 = DHT11 Humitidy and Temperature Sensor
  WeMos_D1_Mini_Relay_Shield_V1 = WeMos D1 Mini Relay Shield V2
  WeMos_D1_Mini_Relay_Shield_V2 = WeMos D1 Mini Relay Shield V2
  WeMos_D1_Mini_Relay_Shield_V3 = WeMos D1 Mini Relay Shield V2
  Nokia_5110_LCD_Module1 = Nokia 5110 LCD
  R4 = Resistor [tolerance=±5% resistance=10k package=THT]
  R5 = Resistor [tolerance=±5% resistance=1k package=THT]
  R6 = Resistor [tolerance=±5% resistance=10k package=THT]
  R7 = Resistor [tolerance=±5% resistance=10k package=THT]
  R8 = Resistor [tolerance=±5% resistance=10k package=THT]
  U1 = POT [package=pot_alpha_rv16af-20]
  R9 = Resistor [tolerance=±5% resistance=330 package=THT]
  Part1 = Arduino Mega 2560 (Rev3)

nets:
  GND: LED1.common_cathode, part.GND, DHT1.GND, DHT2.GND, Nokia_5110_LCD_Module1.LED_(out), U1.A, Part1.GND
  N1: part.RXD, Part1.D7_PWM
  VCC: part.VCC, part.CH_PD, Nokia_5110_LCD_Module1.DN(MODI)_(out), U1.E, Part1.3V3
  N2: part.TXD, Part1.D6_PWM
  N3: R1.Pin_1, Part1.D8_PWM
  N4: R2.Pin_1, Part1.D11_PWM
  N5: R3.Pin_1, Part1.D10_PWM
  VDD: DHT1.VDD, DHT2.VDD, Part1.5V
  N6: DHT1.DATA, Part1.D13_PWM
  N7: DHT2.DATA, Part1.D12_PWM
  N8: WeMos_D1_Mini_Relay_Shield_V1.D1, Part1.D5_PWM
  N9: WeMos_D1_Mini_Relay_Shield_V2.D1, Part1.D4_PWM
  N10: WeMos_D1_Mini_Relay_Shield_V3.D1, Part1.D3_PWM
  N11: Nokia_5110_LCD_Module1.VCC_(out), R4.Pin_1
  N12: Nokia_5110_LCD_Module1.GND_(out), R5.Pin_1
  N13: Nokia_5110_LCD_Module1.SCE_(out), R6.Pin_1
  N14: Nokia_5110_LCD_Module1.RST_(out), R7.Pin_1
  N15: Nokia_5110_LCD_Module1.D/C_(out), R8.Pin_1
  N16: Nokia_5110_LCD_Module1.SCLK_(out), R9.Pin_1
  N17: R4.Pin_0, Part1.D43
  N18: R5.Pin_0, Part1.D44
  N19: R6.Pin_0, Part1.D45
  N20: R7.Pin_0, Part1.D46
  N21: R8.Pin_0, Part1.D47
  N22: U1.S, R9.Pin_0

notes:
  Rx -> Pin 7
  Tx -> Pin 6
  VCC - 3.3V
  Temp Out
  Temp In
  PUMP
  Mst Valve
  Outside Valve
  1K
  10K
  R = 100 - 330 Ohms
  330

custom parts:
  ESP8266 WiFi Module: Generic WiFi Module based on the ESP8266 with onboard PCB antenna and UART communications
  DHT11 Humitidy and Temperature Sensor: DHT11 Humidity and Temperature Sensor
  Nokia 5110 LCD: Nokia 5110 Graphic 84*48 LCD module such as the Sparkfun LCD-10168 or the clones from Ebay. There is example code for the Arduino available from the Sparkfun site in https://learn.sparkfun.com/tutorials/graphic-lcd-hookup-guide This is a 3.3V device, if you are running it from a 5V micro you need a 5V tolorant level translator such as the 74ahc367 to protect the signal imputs. Rafa G. did a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
